# Fritzing sketch KeyFinder (saved by Fritzing 0.9.10b)
breadboards: 1

parts:
  MCU1 = Raspberry Pi Zero
  Part3 = RFID-RC522-v2
  Part4 = RFID-RC522-v2
  Part5 = RFID-RC522-v2

nets:
  GND: MCU1.pin_1, MCU1.pin_17, Part3.GND, Part4.GND, Part5.GND
  N1: MCU1.pin_9, Part3.3_3V, Part4.3_3V, Part5.3_3V
  N2: MCU1.pin_19, Part3.MOSI, Part4.MOSI, Part5.MOSI
  N3: MCU1.pin_21, Part3.MISO, Part4.MISO, Part5.MISO
  N4: MCU1.pin_23, Part3.SCK, Part4.SCK, Part5.SCK
  N5: MCU1.pin_24, Part3.SDA, Part4.SDA, Part5.SDA

custom parts:
  RFID-RC522-v2: A simple China made RFID-RC522 Reader; do check the pin labels, as this is a MFRC522 based clone.
